# Fritzing sketch diagrama-esquematico-saida-4-20mA-Arduino (saved by Fritzing 0.9.2b)

parts:
  Part1 = Arduino Uno (Rev3) - ICSP
  R1 = Resistor [tolerance=±5% resistance=4.7k package="0805 [SMD]"]
  C1 = Capacitor [package=cap-pth-small2]
  Q1 = NPN-Transistor [package="TO92 [THT]"]
  U2 = LMV324 [package=so014]
  R2 = Resistor [tolerance=±5% resistance=10 package="0805 [SMD]"]
  JP1 = Header 2 [package=screwterminal-3.5mm-2_lock]
  R3 = Resistor [tolerance=±5% resistance=150 package=THT]

nets:
  N1: Part1.D9_PWM, R1.Pin_0
  N2: Part1.GND, C1.1, U2.G$1_-V, R3.Pin_1
  N3: Part1.5V, U2.G$1_+V, JP1.2
  N4: R1.Pin_1, C1.2, U2.G$1_+IN
  N5: Q1.E, JP1.1
  N6: Q1.B, R2.Pin_1
  N7: Q1.C, U2.G$1_-IN, R3.Pin_0
  N8: U2.G$1_OUT, R2.Pin_0

notes:
  Saida 4-20mA
  LM224 ou 324
  BC548 (NPN)
  150 ou 180ohm
  10 Ohm
  4700 Ohm
  100 nF
  C
  b
  E
  Referencia de tensao
  Realim.
  GND
  5V
  Saída PWM
